// Logisim project SquareRoot_SingleDataPath_V1.2.circ as structural Verilog: 6 circuits, main circuit Topo
module Topo (
  input  [15:0] Input,
  output ready,
  output [7:0] root
);

  wire clk, controlpath_1_boot, controlpath_1_mux_root, controlpath_1_wr_regs, datapath_1_n, rst;
  wire [10:0] Ciclos_q;

  Clock clock_1 (.out(clk));
  Button button_1 (.out(rst));
  // Probe on Input
  ControlPath controlpath_1 (
    .N(datapath_1_n), .clk(clk), .rst(rst), .boot(controlpath_1_boot), .wr_regs(controlpath_1_wr_regs),
    .mux_root(controlpath_1_mux_root), .ready(ready));
  DataPath datapath_1 (
    .valor(Input), .wr_regs(controlpath_1_wr_regs), .mux_root(controlpath_1_mux_root), .clk(clk),
    .reset(rst), .N(datapath_1_n), .root(root), .boot(controlpath_1_boot));
  // Probe on root
  // Probe on Ciclos_q
  Counter #(.width(11), .max('h7ff)) Ciclos (
    .count(ready), .Q(Ciclos_q), .clk(clk), .clr(rst));  // open: load, D, carry

  // Notes on the sheet:
  //   Ciclos de Clock
endmodule

module DataPath (
  input  [15:0] valor,
  input  boot,
  input  wr_regs,
  input  mux_root,
  input  clk,
  input  reset,
  output N,
  output [7:0] root
);

  wire [0:0] not_1_out;
  wire [7:0] adder_2_out;
  wire [15:0] Input_q;
  wire [16:0] adder_1_out, shifter_1_out, square_q;

  // Probe on valor
  Register #(.width(16)) Input (.D(valor), .en(boot), .Q(Input_q), .clk(clk), .clr(reset));
  Register #(.width(17)) square (.D(adder_1_out), .en(wr_regs), .Q(square_q), .clk(clk), .clr(reset));
  Register u_root (.D(adder_2_out), .en(wr_regs), .Q(root), .clk(clk), .clr(reset));
  Shifter #(.width(17)) shifter_1 (.in({{9{1'b0}}, root}), .\dist (5'b00001), .out(shifter_1_out));
  not not_1 (not_1_out[0], mux_root);
  Comparator #(.width(17), .mode("unsigned")) comparator_1 (.a({1'b0, Input_q}), .b(square_q), .lt(N));  // open: gt, eq
  Adder #(.width(17)) adder_1 (.a(square_q), .b(shifter_1_out), .out(adder_1_out), .cin(1'b1));  // open: cout
  Adder adder_2 (.a(root), .b({{7{mux_root}}, not_1_out[0]}), .out(adder_2_out));  // open: cin, cout
  // Probe on root

  // Other names for the same wires on the sheet: rst = reset
endmodule

module NextStage (
  input  Q1,
  input  Q0,
  input  N,
  output q1_2,
  output q0_2
);

  wire and_1_out;

  and and_1 (and_1_out, Q0, N);
  not not_1 (q0_2, Q1);
  or or_1 (q1_2, and_1_out, Q1);
endmodule

module Outputs (
  input  Q1,
  input  Q0,
  output boot,
  output wr_regs,
  output mux_root,
  output ready
);

  wire not_2_out, not_3_out;

  not not_1 (boot, Q0);
  not not_2 (not_2_out, Q1);
  not not_3 (not_3_out, Q1);
  or or_1 (wr_regs, not_2_out, Q0);
  or or_2 (ready, not_3_out, Q0);

  assign mux_root = Q1;
endmodule

module ControlPath (
  input  N,
  input  clk,
  input  rst,
  output boot,
  output wr_regs,
  output mux_root,
  output ready
);

  wire nextstage_1_q0_2, nextstage_1_q1_2, Q0_q, Q1_q;

  NextStage nextstage_1 (.Q1(Q1_q), .Q0(Q0_q), .N(N), .q1_2(nextstage_1_q1_2), .q0_2(nextstage_1_q0_2));
  D_Flip_Flop Q1 (.clk(clk), .D(nextstage_1_q1_2), .Q(Q1_q), .reset(rst));  // open: Qn, preset, en
  D_Flip_Flop Q0 (.clk(clk), .D(nextstage_1_q0_2), .Q(Q0_q), .reset(rst));  // open: Qn, preset, en
  Outputs outputs_1 (.Q1(Q1_q), .Q0(Q0_q), .boot(boot), .wr_regs(wr_regs), .mux_root(mux_root), .ready(ready));
endmodule

module f (
  input  F,
  output A7,
  output A6,
  output A5,
  output A4,
  output A3,
  output A2,
  output A1,
  output A0
);

  not not_1 (A0, F);

  assign A1 = F;
  assign A2 = F;
  assign A3 = F;
  assign A4 = F;
  assign A5 = F;
  assign A6 = F;
  assign A7 = F;
endmodule
