// Logisim project BubbleSort.circ as structural Verilog: 2 circuits, main circuit main
module main (
  input  mux_in,
  input  wr_last,
  input  wr_bigger,
  input  en_counter,
  input  en_count,
  output eh_maior,
  output end_comp
);

  wire clk, comparator_1_eq, not_1_out, not_2_out, not_3_out, or_1_out, or_2_out, rst;
  wire [3:0] adder_1_out, adder_2_out, multiplexer_3_out, register_12_q, register_13_q;
  wire [7:0] counter_1_q;
  wire [9:0] counter_2_q;
  wire [31:0] multiplexer_1_out, multiplexer_2_out, ram_1_data, register_1_q, register_2_q, register_3_q,
       register_4_q, register_5_q, register_6_q, register_7_q, register_8_q, register_9_q, register_10_q,
       register_11_q;

  Counter counter_1 (.Q(counter_1_q), .clk(clk), .clr(rst));  // open: load, D, count, carry
  Counter #(.width(10), .max('h3ff)) counter_2 (.Q(counter_2_q), .clk(clk), .clr(rst));  // open: load, D, count, carry
  // Probe on counter_2_q
  RAM #(.dataWidth(32)) ram_1 (.addr(counter_1_q), .data(ram_1_data));  // open: sel, clk, ld, clr
  Clock clock_1 (.out(clk));
  Button button_1 (.out(rst));
  not not_1 (not_1_out, en_counter);
  Register #(.width(32)) register_1 (.D(multiplexer_1_out), .Q(register_1_q), .clk(clk), .clr(rst));  // open: en
  Multiplexer #(.width(32)) multiplexer_1 (
    .in0(ram_1_data), .in1(multiplexer_2_out), .out(multiplexer_1_out), .sel(mux_in));  // open: en
  not not_2 (not_2_out, mux_in);
  or or_1 (or_1_out, rst, not_1_out);
  Register #(.width(32)) register_2 (.D(register_1_q), .Q(register_2_q), .clk(clk), .clr(rst));  // open: en
  Register #(.width(32)) register_3 (.D(register_2_q), .Q(register_3_q), .clk(clk), .clr(rst));  // open: en
  or or_2 (or_2_out, not_2_out, wr_bigger);
  Register #(.width(32)) register_4 (.D(register_3_q), .Q(register_4_q), .clk(clk), .clr(rst));  // open: en
  Register #(.width(32)) register_5 (.D(register_4_q), .Q(register_5_q), .clk(clk), .clr(rst));  // open: en
  not not_3 (not_3_out, or_2_out);
  Register #(.width(32)) register_6 (.D(register_7_q), .Q(register_6_q), .clk(clk), .clr(rst));  // open: en
  Register #(.width(32)) register_7 (.D(register_5_q), .Q(register_7_q), .clk(clk), .clr(rst));  // open: en
  Multiplexer #(.width(32)) multiplexer_2 (
    .in0(register_11_q), .in1(register_9_q), .out(multiplexer_2_out), .sel(not_3_out));  // open: en
  Register #(.width(32)) register_8 (.D(register_6_q), .Q(register_8_q), .clk(clk), .clr(rst));  // open: en
  Register #(.width(32)) register_9 (.D(register_8_q), .Q(register_9_q), .clk(clk), .clr(rst));  // open: en
  Register #(.width(32)) register_10 (.D(multiplexer_2_out), .en(wr_last), .Q(register_10_q), .clk(clk), .clr(rst));
  Register #(.width(32)) register_11 (.D(register_9_q), .en(or_2_out), .Q(register_11_q), .clk(clk), .clr(rst));
  Register #(.width(4)) register_12 (.D(adder_1_out), .en(en_counter), .Q(register_12_q), .clk(clk), .clr(or_1_out));
  Register #(.width(4)) register_13 (.D(adder_2_out), .en(en_count), .Q(register_13_q), .clk(clk), .clr(rst));
  Adder #(.width(4)) adder_1 (.a(4'b0001), .b(register_12_q), .out(adder_1_out));  // open: cin, cout
  Comparator #(.width(4)) comparator_1 (
    .a(register_12_q), .b(multiplexer_3_out), .eq(comparator_1_eq));  // open: gt, lt
  Multiplexer #(.width(4)) multiplexer_3 (
    .in0(4'b1001), .in1(register_13_q), .out(multiplexer_3_out), .sel(mux_in));  // open: en
  Adder #(.width(4)) adder_2 (.a(register_13_q), .b(4'b0001), .out(adder_2_out));  // open: cin, cout
  Comparator #(.width(32)) comparator_2 (.a(register_11_q), .b(register_9_q), .lt(eh_maior));  // open: gt, eq
  Comparator #(.width(32)) comparator_3 (.a(register_9_q), .b(register_10_q), .eq(end_comp));  // open: gt, lt
endmodule

module g (
  input  en_sr,
  input  mux_in,
  input  wr_last,
  input  wr_bigger,
  input  wr_first,
  input  en_counter,
  input  rst_counter,
  output eh_maior,
  output end_comp,
  output end_comp_2,
  output count
);

  wire clk, not_1_out, rst;
  wire [3:0] counter_3_q;
  wire [7:0] counter_1_q;
  wire [9:0] counter_2_q;
  wire [31:0] multiplexer_1_out, multiplexer_2_out, ram_1_data, register_1_q, register_2_q, register_3_q,
       register_4_q, register_5_q, register_6_q, register_7_q, register_8_q, register_9_q, register_10_q,
       register_11_q, register_12_q;

  Counter counter_1 (.Q(counter_1_q), .clk(clk), .clr(rst));  // open: load, D, count, carry
  Counter #(.width(10), .max('h3ff)) counter_2 (.Q(counter_2_q), .clk(clk), .clr(rst));  // open: load, D, count, carry
  // Probe on counter_2_q
  RAM #(.dataWidth(32)) ram_1 (.addr(counter_1_q), .data(ram_1_data));  // open: sel, clk, ld, clr
  Clock clock_1 (.out(clk));
  Button button_1 (.out(rst));
  Multiplexer #(.width(32)) multiplexer_1 (
    .in0(ram_1_data), .in1(multiplexer_2_out), .out(multiplexer_1_out), .sel(mux_in));  // open: en
  Register #(.width(32)) register_1 (.D(multiplexer_1_out), .en(en_sr), .Q(register_1_q), .clk(clk), .clr(rst));
  Register #(.width(32)) register_2 (.D(register_3_q), .en(en_sr), .Q(register_2_q), .clk(clk), .clr(rst));
  Register #(.width(32)) register_3 (.D(register_1_q), .en(en_sr), .Q(register_3_q), .clk(clk), .clr(rst));
  Register #(.width(32)) register_4 (.D(register_5_q), .en(en_sr), .Q(register_4_q), .clk(clk), .clr(rst));
  Register #(.width(32)) register_5 (.D(register_2_q), .en(en_sr), .Q(register_5_q), .clk(clk), .clr(rst));
  not not_1 (not_1_out, wr_bigger);
  Register #(.width(32)) register_6 (.D(register_7_q), .en(en_sr), .Q(register_6_q), .clk(clk), .clr(rst));
  Register #(.width(32)) register_7 (.D(register_4_q), .en(en_sr), .Q(register_7_q), .clk(clk), .clr(rst));
  Multiplexer #(.width(32)) multiplexer_2 (
    .in0(register_12_q), .in1(register_9_q), .out(multiplexer_2_out), .sel(not_1_out));  // open: en
  Register #(.width(32)) register_8 (.D(register_6_q), .en(en_sr), .Q(register_8_q), .clk(clk), .clr(rst));
  Register #(.width(32)) register_9 (.D(register_8_q), .en(en_sr), .Q(register_9_q), .clk(clk), .clr(rst));
  Register #(.width(32)) register_10 (.D(multiplexer_2_out), .en(wr_last), .Q(register_10_q), .clk(clk), .clr(rst));
  Register #(.width(32)) register_11 (.D(multiplexer_2_out), .en(wr_first), .Q(register_11_q), .clk(clk), .clr(rst));
  Counter #(.width(4), .max('hf)) counter_3 (
    .count(en_counter), .Q(counter_3_q), .clk(clk), .clr(rst_counter));  // open: load, D, carry
  Register #(.width(32)) register_12 (.D(register_9_q), .en(wr_bigger), .Q(register_12_q), .clk(clk), .clr(rst));
  Comparator #(.width(32)) comparator_1 (.a(register_12_q), .b(register_9_q), .lt(eh_maior));  // open: gt, eq
  Comparator #(.width(32)) comparator_2 (.a(register_9_q), .b(register_10_q), .eq(end_comp));  // open: gt, lt
  Comparator #(.width(32)) comparator_3 (.a(register_12_q), .b(register_11_q), .eq(end_comp_2));  // open: gt, lt
  Comparator #(.width(4)) comparator_4 (.a(4'b1001), .b(counter_3_q), .eq(count));  // open: gt, lt
endmodule
